// Logisim project 1ejercicio.circ as structural Verilog: 1 circuit, main circuit main
module main (
  input  A,
  input  B,
  input  C
);

  wire and_1_out, not_1_out, not_2_out, not_3_out, or_1_out, or_2_out;

  not not_1 (not_1_out, B);
  not not_2 (not_2_out, A);
  not not_3 (not_3_out, B);
  or or_1 (or_1_out, A, not_1_out, C);
  or or_2 (or_2_out, not_2_out, not_3_out, C);
  LED led_1 (.in(and_1_out));
  and and_1 (and_1_out, or_1_out, or_2_out);
endmodule
