// Logisim project 3ejercicio.circ as structural Verilog: 1 circuit, main circuit main
module main (
  input  A,
  input  B,
  input  C,
  input  D
);

  wire and_1_out, nand_1_out, not_1_out, or_1_out;

  and and_1 (and_1_out, A, not_1_out, C);
  not not_1 (not_1_out, B);
  nand nand_1 (nand_1_out, C, D);
  or or_1 (or_1_out, A, and_1_out, nand_1_out);
  LED led_1 (.in(or_1_out));
endmodule
