// Logisim project ejer10A.circ as structural Verilog: 1 circuit, main circuit main
module main (
  input  A,
  input  B
);

  wire not_1_out, or_1_out;

  not not_1 (not_1_out, A);
  or or_1 (or_1_out, not_1_out, B);
  LED led_1 (.in(or_1_out));

  // Notes on the sheet:
  //   F
endmodule
