// Logisim project ejer10B.circ as structural Verilog: 1 circuit, main circuit main
module main (
  input  A,
  input  B
);

  wire and_1_out, not_1_out;

  not not_1 (not_1_out, B);
  and and_1 (and_1_out, A, not_1_out);
  LED led_1 (.in(and_1_out));

  // Notes on the sheet:
  //   G
endmodule
