// Logisim project ejer3.circ as structural Verilog: 1 circuit, main circuit main
module main (
  input  X,
  input  Y,
  input  Z
);

  wire and_1_out, and_2_out, and_3_out, not_1_out, not_2_out, or_1_out;

  and and_1 (and_1_out, Y, X);
  and and_2 (and_2_out, Z, Y);
  and and_3 (and_3_out, Z, not_1_out, not_2_out);
  not not_1 (not_1_out, Y);
  not not_2 (not_2_out, X);
  or or_1 (or_1_out, and_1_out, and_2_out, and_3_out);
  LED led_1 (.in(or_1_out));
endmodule
