// Logisim project ejer5B.circ as structural Verilog: 1 circuit, main circuit main
module main (
  input  A,
  input  A_2,
  input  B,
  input  B_2
);

  wire nand_1_out, not_1_out, not_2_out, or_1_out;

  nand nand_1 (nand_1_out, A, B);
  LED led_1 (.in(nand_1_out));
  not not_1 (not_1_out, A_2);
  not not_2 (not_2_out, B_2);
  LED led_2 (.in(or_1_out));
  or or_1 (or_1_out, not_1_out, not_2_out);

  // Notes on the sheet:
  //   (A * B)'
  //   A'+B'
endmodule
