// Logisim project ejer5C.circ as structural Verilog: 1 circuit, main circuit main
module main (
  input  A,
  input  A_2,
  input  B,
  input  B_2
);

  wire and_1_out, nor_1_out, not_1_out, not_2_out;

  not not_1 (not_1_out, A);
  nor nor_1 (nor_1_out, not_1_out, B);
  LED led_1 (.in(nor_1_out));
  not not_2 (not_2_out, B_2);
  LED led_2 (.in(and_1_out));
  and and_1 (and_1_out, A_2, not_2_out);

  // Notes on the sheet:
  //   (A’ + B)’
  //   A * B’
endmodule
