// Logisim project ejer5D.circ as structural Verilog: 1 circuit, main circuit main
module main (
  input  E,
  input  E_2,
  input  B,
  input  B_2
);

  wire nand_1_out, not_1_out, not_2_out, or_1_out;

  not not_1 (not_1_out, E);
  not not_2 (not_2_out, B);
  nand nand_1 (nand_1_out, not_1_out, not_2_out);
  LED led_1 (.in(nand_1_out));
  LED led_2 (.in(or_1_out));
  or or_1 (or_1_out, E_2, B_2);

  // Notes on the sheet:
  //   (E’ * B’)’ 
  //   E + B
endmodule
