// Logisim project ejer8mini.circ as structural Verilog: 1 circuit, main circuit main
module main (
  input  x,
  input  y,
  input  z
);

  wire and_1_out, not_1_out, not_2_out, or_1_out;

  not not_1 (not_1_out, z);
  or or_1 (or_1_out, not_1_out, y, z);
  not not_2 (not_2_out, x);
  LED led_1 (.in(and_1_out));
  and and_1 (and_1_out, or_1_out, not_2_out);

  // Notes on the sheet:
  //   Minitérminos en R1
  //   R1
endmodule
