// Logisim project ejerA.circ as structural Verilog: 1 circuit, main circuit main
module main (
  input  X,
  input  Y
);

  wire and_1_out, not_1_out, or_1_out;

  not not_1 (not_1_out, X);
  or or_1 (or_1_out, not_1_out, Y);
  and and_1 (and_1_out, X, or_1_out);
  LED led_1 (.in(and_1_out));
endmodule
