// Logisim project ejerC.circ as structural Verilog: 1 circuit, main circuit main
module main (
  input  X,
  input  Y,
  input  Z
);

  wire and_1_out, and_2_out, not_1_out, or_1_out, or_2_out;

  not not_1 (not_1_out, X);
  and and_1 (and_1_out, X, Y);
  and and_2 (and_2_out, Z, or_1_out);
  or or_1 (or_1_out, not_1_out, Y);
  LED led_1 (.in(or_2_out));
  or or_2 (or_2_out, and_1_out, and_2_out);
endmodule
